// Logisim project ex6.circ as structural Verilog: 5 circuits, main circuit RotRight
module RotRight (
  input  [15:0] INPUT0,
  input  [3:0] AMOUNT,
  output [15:0] OUTPUT0
);

  wire [15:0] rot1_1_out_2, rot2_1_out_2, rot4_1_out_2, rot8_1_out_2, T1, T2, T3;

  rot8 rot8_1 (.out_2(rot8_1_out_2), .in_1(INPUT0));
  rot4 rot4_1 (.out_2(rot4_1_out_2), .in_1(T1));
  Multiplexer #(.enable("false"), .width(16)) multiplexer_1 (
    .in0(INPUT0), .in1(rot8_1_out_2), .out(T1), .sel(AMOUNT[3]));
  Multiplexer #(.enable("false"), .width(16)) multiplexer_2 (.in0(T1), .in1(rot4_1_out_2), .out(T2), .sel(AMOUNT[2]));
  rot2 rot2_1 (.out_2(rot2_1_out_2), .in_1(T2));
  Multiplexer #(.enable("false"), .width(16)) multiplexer_3 (.in0(T2), .in1(rot2_1_out_2), .out(T3), .sel(AMOUNT[1]));
  rot1 rot1_1 (.out_2(rot1_1_out_2), .in_1(T3));
  Multiplexer #(.enable("false"), .width(16)) multiplexer_4 (
    .in0(T3), .in1(rot1_1_out_2), .out(OUTPUT0), .sel(AMOUNT[0]));

  // Other names for the same wires on the sheet: T[15:0] = INPUT0; T4[15:0] = OUTPUT0
endmodule

module rot1 (
  input  [15:0] in_1,
  output [15:0] out_2
);


  assign out_2 = {in_1[0], in_1[15:1]};
endmodule

module rot2 (
  input  [15:0] in_1,
  output [15:0] out_2
);


  assign out_2 = {in_1[1:0], in_1[15:2]};
endmodule

module rot4 (
  input  [15:0] in_1,
  output [15:0] out_2
);


  assign out_2 = {in_1[3:0], in_1[15:4]};
endmodule

module rot8 (
  input  [15:0] in_1,
  output [15:0] out_2
);


  assign out_2 = {in_1[7:0], in_1[15:8]};
endmodule
